# Fritzing sketch schematic (saved by Fritzing 0.9.9b)
breadboards: 1

parts:
  Part1 = Arduino MKR WiFi 1010
  NEOPIXEL1 = Neopixel Strip -- Black (30/m) [part_number=1376]
  Part2 = Adafruit LSM9DS1 9DoF Breakout [part_number="Adafruit #3387"]
  Part3 = LilyPad Buzzer
  BAT1 = Battery Holders [package=battcon_20mm_4legs]

nets:
  +5V: Part1.AREF, NEOPIXEL1.+5V, Part2.VDD, BAT1.-
  GND: Part1.A0_DAC0, NEOPIXEL1.GND, Part2.GND, Part3.-, BAT1.+
  N1: Part1.A2, Part2.SCL
  N2: Part1.A4, Part2.SDA
  N3: Part1.A5, NEOPIXEL1.Din
  N4: Part1.RESET, Part3.+

notes:
  vibration motor
  IMU (I2C)
  Battery
  external LEDs

custom parts:
  Arduino MKR WiFi 1010: This is the newest version of the MKR 1000 WIFI, but with an ESP32 module on board made by U-BLOX.
  Neopixel Strip -- Black (30/m): These NeoPixel strips have 30 digitally-addressable pixel LEDs per meter and are very affordable and are only 12.5 mm wide, 10 mm if you remove the strip from the casing.
  Adafruit LSM9DS1 9DoF Breakout: Add motion, direction and orientation sensing to your Arduino project with this all-in-one 9-DOF sensor. Inside the chip are three sensors, one is a classic 3-axis accelerometer, which can tell you which direction is down towards the Earth (by measuring gravity) or how fast the board is accelerating in 3D space. The other is a 3-axis magnetometer that can sense where the strongest magnetic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
